# Fritzing sketch hand (saved by Fritzing 1.0.7)
breadboards: 1

parts:
  ESP1 = ESP32-DevkitC
  VCC1 = 4 x AAA Battery Mount [internal_resistance=0.1Ω]
  パーツ1 = Adafruit PCA9685 PWM/Servo Breakout [part_number=815]
  J1 = Basic Servo
  J2 = Basic Servo

nets:
  GND: ESP1.GND, VCC1.-, パーツ1.GND, J1.pulse, J2.pulse
  N1: ESP1.IO19, パーツ1.SCL
  N2: ESP1.IO18, パーツ1.SDA
  5V: ESP1.5V, パーツ1.VCC
  VCC: VCC1.+, パーツ1.5.0V, J1.vcc, J2.vcc
  N3: パーツ1.PWM1, J2.gnd
  N4: パーツ1.PWM0, J1.gnd
