# Fritzing sketch tt_motor (saved by Fritzing 1.0.7)
breadboards: 2

parts:
  ESP1 = ESP32-DevkitC
  VCC1 = 4 x AAA Battery Mount [internal_resistance=0.1Ω]
  パーツ1 = Motor Driver 1A Dual TB6612FNG  # not connected
  M1 = gear-motor  # not connected
  M2 = gear-motor  # not connected

nets:
  N1: ESP1.GND, VCC1.-
